// Logisim project Common bus system CA.circ as structural Verilog: 1 circuit, main circuit main
module main (
  input  [3:0] in_1,
  input  in_2,
  input  in_3,
  input  in_4,
  input  in_5,
  input  [1:0] in_6,
  input  in_7,
  output [3:0] out_8,
  output out_9,
  output out_10,
  output [3:0] out_11,
  output out_12,
  output out_13
);

  wire clock_1_out;
  wire [3:0] register_2_q, register_3_q, register_4_q;

  Clock clock_1 (.out(clock_1_out));
  Register #(.width(4)) register_1 (.D(in_1), .en(in_2), .Q(out_8), .clk(clock_1_out), .clr(in_7));
  Register #(.width(4)) register_2 (
    .D({out_11[3:2], out_10, out_9}), .en(in_3), .Q(register_2_q), .clk(clock_1_out), .clr(in_7));
  Register #(.width(4)) register_3 (
    .D({out_11[3:2], out_10, out_9}), .en(in_4), .Q(register_3_q), .clk(clock_1_out), .clr(in_7));
  Register #(.width(4)) register_4 (
    .D({out_11[3:2], out_10, out_9}), .en(in_5), .Q(register_4_q), .clk(clock_1_out), .clr(in_7));
  Multiplexer #(.select(2)) multiplexer_1 (
    .in0(out_8[0]), .in1(register_2_q[0]), .in2(register_3_q[0]), .in3(register_4_q[0]), .out(out_9),
    .sel(in_6));  // open: en
  Multiplexer #(.select(2)) multiplexer_2 (
    .in0(out_8[1]), .in1(register_2_q[1]), .in2(register_3_q[1]), .in3(register_4_q[1]), .out(out_10),
    .sel(in_6));  // open: en
  Multiplexer #(.select(2)) multiplexer_3 (
    .in0(out_8[2]), .in1(register_2_q[2]), .in2(register_3_q[2]), .in3(register_4_q[2]), .out(out_11[2]),
    .sel(in_6));  // open: en
  Multiplexer #(.select(2)) multiplexer_4 (
    .in0(out_8[3]), .in1(register_2_q[3]), .in2(register_3_q[3]), .in3(register_4_q[3]), .out(out_11[3]),
    .sel(in_6));  // open: en

  assign out_11[1:0] = {out_10, out_9};
  assign out_12 = out_11[2];
  assign out_13 = out_11[3];

  // Notes on the sheet:
  //   Common bus system using multiplexer
endmodule
